// Logisim project ALU.circ as structural Verilog: 3 circuits, main circuit main
module main (
  input  [7:0] a8,
  input  [7:0] b8,
  input  x,
  input  y,
  input  z,
  output [7:0] alu_out,
  output tmp_C
);

  wire abext_1_c_out, abext_1_o_x, abext_1_o_y, abext_1_o_z;
  wire [7:0] abext_1_o_a, abext_1_o_b;

  // NoConnect on abext_1_o_x
  abext abext_1 (
    .a8(a8), .b8(b8), .i_x(x), .i_y(y), .i_z(z), .o_x(abext_1_o_x), .o_y(abext_1_o_y), .o_z(abext_1_o_z),
    .o_a(abext_1_o_a), .o_b(abext_1_o_b), .c_out(abext_1_c_out));
  // NoConnect on abext_1_o_y
  // NoConnect on abext_1_o_z
  Adder adder_1 (.a(abext_1_o_a), .b(abext_1_o_b), .out(alu_out), .cin(abext_1_c_out), .cout(tmp_C));
endmodule

module adder_8b (
  input  b1_7,
  input  b1_6,
  input  b1_5,
  input  b1_4,
  input  b1_3,
  input  b1_2,
  input  b1_1,
  input  b1_0,
  input  b2_7,
  input  b2_6,
  input  b2_5,
  input  b2_4,
  input  b2_3,
  input  b2_2,
  input  b2_1,
  input  b2_0,
  input  c_in,
  output o_c,
  output o_7,
  output o_6,
  output o_5,
  output o_4,
  output o_3,
  output o_2,
  output o_1,
  output o_0
);

  wire and_1_out, and_2_out, and_3_out, and_4_out, and_5_out, and_6_out, and_7_out, and_8_out, and_9_out,
       and_10_out, and_11_out, and_12_out, and_13_out, and_14_out, and_15_out, and_16_out, not_1_out,
       not_2_out, not_3_out, not_4_out, not_5_out, not_6_out, not_7_out, not_8_out, or_1_out, or_2_out,
       or_4_out, or_5_out, or_6_out, or_7_out, or_8_out, or_9_out, or_10_out, or_11_out, or_12_out,
       or_13_out, or_14_out, or_15_out, or_16_out;

  xor xor_1 (o_3, b1_3, or_5_out, b2_3);
  and and_1 (and_1_out, or_5_out, b2_3, b1_3);
  or or_1 (or_1_out, and_1_out, and_2_out);
  xor xor_2 (o_7, b1_7, or_8_out, b2_7);
  or or_2 (or_2_out, or_5_out, b2_3, b1_3);
  not not_1 (not_1_out, o_3);
  and and_2 (and_2_out, not_1_out, or_2_out);
  and and_3 (and_3_out, or_8_out, b2_7, b1_7);
  or or_3 (o_c, and_3_out, and_4_out);
  xor xor_3 (o_2, b1_2, or_10_out, b2_2);
  or or_4 (or_4_out, or_8_out, b2_7, b1_7);
  not not_2 (not_2_out, o_7);
  and and_4 (and_4_out, not_2_out, or_4_out);
  xor xor_4 (o_6, b1_6, or_11_out, b2_6);
  and and_5 (and_5_out, or_10_out, b2_2, b1_2);
  not not_3 (not_3_out, o_2);
  or or_5 (or_5_out, and_5_out, and_6_out);
  or or_6 (or_6_out, or_10_out, b2_2, b1_2);
  and and_6 (and_6_out, not_3_out, or_6_out);
  and and_7 (and_7_out, or_11_out, b2_6, b1_6);
  or or_7 (or_7_out, or_11_out, b2_6, b1_6);
  not not_4 (not_4_out, o_6);
  or or_8 (or_8_out, and_7_out, and_8_out);
  and and_8 (and_8_out, not_4_out, or_7_out);
  xor xor_5 (o_1, b1_1, or_13_out, b2_1);
  xor xor_6 (o_5, b1_5, or_15_out, b2_5);
  and and_9 (and_9_out, or_13_out, b2_1, b1_1);
  or or_9 (or_9_out, or_13_out, b2_1, b1_1);
  not not_5 (not_5_out, o_1);
  or or_10 (or_10_out, and_9_out, and_10_out);
  and and_10 (and_10_out, not_5_out, or_9_out);
  and and_11 (and_11_out, or_15_out, b2_5, b1_5);
  or or_11 (or_11_out, and_11_out, and_12_out);
  or or_12 (or_12_out, or_15_out, b2_5, b1_5);
  not not_6 (not_6_out, o_5);
  and and_12 (and_12_out, not_6_out, or_12_out);
  xor xor_7 (o_0, b1_0, c_in, b2_0);
  xor xor_8 (o_4, b1_4, or_1_out, b2_4);
  and and_13 (and_13_out, c_in, b2_0, b1_0);
  or or_13 (or_13_out, and_13_out, and_14_out);
  or or_14 (or_14_out, c_in, b2_0, b1_0);
  not not_7 (not_7_out, o_0);
  and and_14 (and_14_out, not_7_out, or_14_out);
  and and_15 (and_15_out, or_1_out, b2_4, b1_4);
  not not_8 (not_8_out, o_4);
  or or_15 (or_15_out, and_15_out, and_16_out);
  or or_16 (or_16_out, or_1_out, b2_4, b1_4);
  and and_16 (and_16_out, not_8_out, or_16_out);

  // Notes on the sheet:
  //   b1_7
  //   b1_6
  //   8-bit adder (No half adder, w/ 0-input)
  //   b1_5
  //   b1_4
  //   o_4
  //   o_7
  //   b1_3
  //   b1_2
  //   b1_1
  //   b1_0
  //   o_3
  //   o_6
  //   o_2
  //   b2_7
  //   b2_6
  //   o_5
  //   b2_5
  //   b2_4
  //   b2_3
  //   b2_2
  //   o_1
  //   b2_1
  //   b2_0
  //   o_4
  //   c_in
endmodule

module abext (
  input  [7:0] a8,
  input  [7:0] b8,
  input  i_x,
  input  i_y,
  input  i_z,
  output o_x,
  output o_y,
  output o_z,
  output [7:0] o_a,
  output [7:0] o_b,
  output c_out
);

  wire [7:0] nand_100_out, not_1_out, not_2_out, shifter_1_out, shifter_2_out, xor_101_out;

  assign not_1_out = ~b8;  // NOT_Gate not_1, 8 bits wide
  assign nand_100_out = ~(a8 & b8);  // NAND_Gate nand_100, 8 bits wide
  assign xor_101_out = a8 ^ b8;  // XOR_Gate xor_101, 8 bits wide
  Multiplexer #(.select(3), .width(16)) multiplexer_1 (
    .in0({not_1_out, a8}), .in1({a8, a8}), .in2({{8{1'b0}}, shifter_1_out}),
    .in3({{8{1'b0}}, shifter_2_out}), .in4({{8{1'b0}}, nand_100_out}), .in5({{8{1'b0}}, xor_101_out}),
    .in6({{8{1'b0}}, a8[0], a8[1], a8[2], a8[3], a8[4], a8[5], a8[6], a8[7]}), .in7({{8{1'b0}}, not_2_out}),
    .out({o_b, o_a}), .sel({i_x, i_y, i_z}));
  Shifter shifter_1 (.in(a8), .\dist (3'b011), .out(shifter_1_out));
  Shifter #(.shift("lr")) shifter_2 (.in(a8), .\dist (3'b011), .out(shifter_2_out));
  nor nor_1 (c_out, i_z, i_y, i_x);
  assign not_2_out = ~a8;  // NOT_Gate not_2, 8 bits wide

  assign o_x = i_x;
  assign o_y = i_y;
  assign o_z = i_z;

  // Notes on the sheet:
  //   a-b = 000, invert
  //   a+b = 001 noop
  //   a*8 = 010 lshift
  //   a/8 = 011 rshift
  //   bit reversal 110
  //   bit complement 111
endmodule
