// Logisim project adder.circ as structural Verilog: 2 circuits, main circuit main
module main (
  input  b1,
  input  b2,
  input  b1_2,
  input  b2_2,
  input  c,
  input  in_6,
  input  in_7,
  input  in_8,
  input  in_9,
  input  in_10,
  input  in_11,
  input  in_12,
  input  in_13,
  input  in_14,
  input  in_15,
  input  in_16,
  input  in_17,
  input  in_18,
  input  in_19,
  input  in_20,
  input  in_21,
  input  in_22,
  input  in_23,
  input  in_24,
  input  in_25,
  input  in_26,
  input  in_27,
  input  in_28,
  input  in_29,
  input  in_30,
  input  in_31,
  input  in_32,
  input  in_33,
  input  in_34,
  input  in_35,
  input  in_36,
  input  in_37,
  output out,
  output out_39,
  output out_40,
  output out_41,
  output out_42,
  output out_43,
  output out_44,
  output out_45,
  output out_46,
  output out_47,
  output out_48,
  output out_49,
  output out_50
);

  wire adder_8b_2_o_0, adder_8b_2_o_1, adder_8b_2_o_2, adder_8b_2_o_3, adder_8b_2_o_4, adder_8b_2_o_5,
       adder_8b_2_o_6, adder_8b_2_o_7, adder_8b_2_o_c, adder_8b_3_o_0, adder_8b_3_o_1, adder_8b_3_o_2,
       adder_8b_3_o_3, adder_8b_3_o_4, adder_8b_3_o_5, adder_8b_3_o_6, adder_8b_3_o_7, adder_8b_3_o_c,
       and_2_out, and_3_out, not_1_out, or_1_out;

  xor xor_1 (out, b2, b1);
  xor xor_2 (out_40, b1_2, c, b2_2);
  and and_1 (out_39, b2, b1);
  and and_2 (and_2_out, c, b2_2, b1_2);
  or or_1 (or_1_out, c, b2_2, b1_2);
  not not_1 (not_1_out, out_40);
  or or_2 (out_41, and_2_out, and_3_out);
  and and_3 (and_3_out, not_1_out, or_1_out);
  adder_8b adder_8b_1 (
    .b1_7(adder_8b_3_o_7), .b1_6(adder_8b_3_o_6), .b1_5(adder_8b_3_o_5), .b1_4(adder_8b_3_o_4),
    .b1_3(adder_8b_3_o_3), .b1_2(adder_8b_3_o_2), .b1_1(adder_8b_3_o_1), .b1_0(adder_8b_3_o_0), .b2_7(in_37),
    .b2_6(in_36), .b2_5(in_35), .b2_4(in_34), .b2_3(in_33), .b2_2(in_32), .b2_1(in_31), .b2_0(in_30),
    .c_in(adder_8b_3_o_c), .o_c(out_50), .o_7(out_49), .o_6(out_48), .o_5(out_47), .o_4(out_46),
    .o_3(out_45), .o_2(out_44), .o_1(out_43), .o_0(out_42));
  adder_8b adder_8b_2 (
    .b1_7(in_13), .b1_6(in_12), .b1_5(in_11), .b1_4(in_10), .b1_3(in_9), .b1_2(in_8), .b1_1(in_7),
    .b1_0(in_6), .b2_7(in_21), .b2_6(in_20), .b2_5(in_19), .b2_4(in_18), .b2_3(in_17), .b2_2(in_16),
    .b2_1(in_15), .b2_0(in_14), .c_in(1'b0), .o_c(adder_8b_2_o_c), .o_7(adder_8b_2_o_7),
    .o_6(adder_8b_2_o_6), .o_5(adder_8b_2_o_5), .o_4(adder_8b_2_o_4), .o_3(adder_8b_2_o_3),
    .o_2(adder_8b_2_o_2), .o_1(adder_8b_2_o_1), .o_0(adder_8b_2_o_0));
  adder_8b adder_8b_3 (
    .b1_7(adder_8b_2_o_7), .b1_6(adder_8b_2_o_6), .b1_5(adder_8b_2_o_5), .b1_4(adder_8b_2_o_4),
    .b1_3(adder_8b_2_o_3), .b1_2(adder_8b_2_o_2), .b1_1(adder_8b_2_o_1), .b1_0(adder_8b_2_o_0), .b2_7(in_29),
    .b2_6(in_28), .b2_5(in_27), .b2_4(in_26), .b2_3(in_25), .b2_2(in_24), .b2_1(in_23), .b2_0(in_22),
    .c_in(adder_8b_2_o_c), .o_c(adder_8b_3_o_c), .o_7(adder_8b_3_o_7), .o_6(adder_8b_3_o_6),
    .o_5(adder_8b_3_o_5), .o_4(adder_8b_3_o_4), .o_3(adder_8b_3_o_3), .o_2(adder_8b_3_o_2),
    .o_1(adder_8b_3_o_1), .o_0(adder_8b_3_o_0));

  // Notes on the sheet:
  //   Half Adder
  //   Full Adder
  //   out
  //   carry
  //   Worst case time: max(5,2) = 5 ns
  //   XOR
  //   carry
  //   Worst case time: max(5, max(2+2,5+1+2+2)) = 10 ns
  //   (see rightmost logic) XOR -> NOT -> AND -> OR
  //   Runtime = 8*max(full) = 80ns
endmodule

module adder_8b (
  input  b1_7,
  input  b1_6,
  input  b1_5,
  input  b1_4,
  input  b1_3,
  input  b1_2,
  input  b1_1,
  input  b1_0,
  input  b2_7,
  input  b2_6,
  input  b2_5,
  input  b2_4,
  input  b2_3,
  input  b2_2,
  input  b2_1,
  input  b2_0,
  input  c_in,
  output o_c,
  output o_7,
  output o_6,
  output o_5,
  output o_4,
  output o_3,
  output o_2,
  output o_1,
  output o_0
);

  wire and_1_out, and_2_out, and_3_out, and_4_out, and_5_out, and_6_out, and_7_out, and_8_out, and_9_out,
       and_10_out, and_11_out, and_12_out, and_13_out, and_14_out, and_15_out, and_16_out, not_1_out,
       not_2_out, not_3_out, not_4_out, not_5_out, not_6_out, not_7_out, not_8_out, or_1_out, or_2_out,
       or_4_out, or_5_out, or_6_out, or_7_out, or_8_out, or_9_out, or_10_out, or_11_out, or_12_out,
       or_13_out, or_14_out, or_15_out, or_16_out;

  xor xor_1 (o_3, b1_3, or_5_out, b2_3);
  and and_1 (and_1_out, or_5_out, b2_3, b1_3);
  or or_1 (or_1_out, and_1_out, and_2_out);
  xor xor_2 (o_7, b1_7, or_8_out, b2_7);
  or or_2 (or_2_out, or_5_out, b2_3, b1_3);
  not not_1 (not_1_out, o_3);
  and and_2 (and_2_out, not_1_out, or_2_out);
  and and_3 (and_3_out, or_8_out, b2_7, b1_7);
  or or_3 (o_c, and_3_out, and_4_out);
  xor xor_3 (o_2, b1_2, or_10_out, b2_2);
  or or_4 (or_4_out, or_8_out, b2_7, b1_7);
  not not_2 (not_2_out, o_7);
  and and_4 (and_4_out, not_2_out, or_4_out);
  xor xor_4 (o_6, b1_6, or_11_out, b2_6);
  and and_5 (and_5_out, or_10_out, b2_2, b1_2);
  not not_3 (not_3_out, o_2);
  or or_5 (or_5_out, and_5_out, and_6_out);
  or or_6 (or_6_out, or_10_out, b2_2, b1_2);
  and and_6 (and_6_out, not_3_out, or_6_out);
  and and_7 (and_7_out, or_11_out, b2_6, b1_6);
  or or_7 (or_7_out, or_11_out, b2_6, b1_6);
  not not_4 (not_4_out, o_6);
  or or_8 (or_8_out, and_7_out, and_8_out);
  and and_8 (and_8_out, not_4_out, or_7_out);
  xor xor_5 (o_1, b1_1, or_13_out, b2_1);
  xor xor_6 (o_5, b1_5, or_15_out, b2_5);
  and and_9 (and_9_out, or_13_out, b2_1, b1_1);
  or or_9 (or_9_out, or_13_out, b2_1, b1_1);
  not not_5 (not_5_out, o_1);
  or or_10 (or_10_out, and_9_out, and_10_out);
  and and_10 (and_10_out, not_5_out, or_9_out);
  and and_11 (and_11_out, or_15_out, b2_5, b1_5);
  or or_11 (or_11_out, and_11_out, and_12_out);
  or or_12 (or_12_out, or_15_out, b2_5, b1_5);
  not not_6 (not_6_out, o_5);
  and and_12 (and_12_out, not_6_out, or_12_out);
  xor xor_7 (o_0, b1_0, c_in, b2_0);
  xor xor_8 (o_4, b1_4, or_1_out, b2_4);
  and and_13 (and_13_out, c_in, b2_0, b1_0);
  or or_13 (or_13_out, and_13_out, and_14_out);
  or or_14 (or_14_out, c_in, b2_0, b1_0);
  not not_7 (not_7_out, o_0);
  and and_14 (and_14_out, not_7_out, or_14_out);
  and and_15 (and_15_out, or_1_out, b2_4, b1_4);
  not not_8 (not_8_out, o_4);
  or or_15 (or_15_out, and_15_out, and_16_out);
  or or_16 (or_16_out, or_1_out, b2_4, b1_4);
  and and_16 (and_16_out, not_8_out, or_16_out);

  // Notes on the sheet:
  //   b1_7
  //   b1_6
  //   8-bit adder (No half adder, w/ 0-input)
  //   b1_5
  //   b1_4
  //   o_4
  //   o_7
  //   b1_3
  //   b1_2
  //   b1_1
  //   b1_0
  //   o_3
  //   o_6
  //   o_2
  //   b2_7
  //   b2_6
  //   o_5
  //   b2_5
  //   b2_4
  //   b2_3
  //   b2_2
  //   o_1
  //   b2_1
  //   b2_0
  //   o_4
  //   c_in
endmodule
