// Logisim project comparator.circ as structural Verilog: 4 circuits, main circuit main
module main (
  input  [15:0] A,
  input  [15:0] B,
  output [15:0] MAX
);

  wire cmp_16bit_1_o_eq, cmp_16bit_1_o_gt, cmp_16bit_1_o_lt;

  // NoConnect on cmp_16bit_1_o_gt
  cmp_16bit cmp_16bit_1 (
    .c1(B), .c0(A), .i_gt(1'b0), .i_eq(1'b0), .i_lt(1'b0), .o_gt(cmp_16bit_1_o_gt), .o_eq(cmp_16bit_1_o_eq),
    .o_lt(cmp_16bit_1_o_lt));
  // NoConnect on cmp_16bit_1_o_eq
  Multiplexer #(.width(16)) multiplexer_1 (.in0(A), .in1(B), .out(MAX), .sel(cmp_16bit_1_o_lt));

  // Notes on the sheet:
  //   16 bit max
endmodule

module cmp_1bit (
  input  c0,
  input  c1,
  input  i_gt,
  input  i_eq,
  input  i_lt,
  output o_gt,
  output o_eq,
  output o_lt
);

  wire eq_out, not_1_out, not_2_out;
  wire [2:0] lt_out;

  not not_1 (not_1_out, c0);
  not not_2 (not_2_out, c1);
  xor eq (eq_out, c0, c1);
  not not_3 (lt_out[1], eq_out);
  and gt (lt_out[2], not_1_out, c1);
  and lt (lt_out[0], c0, not_2_out);
  Multiplexer #(.select(3), .width(3)) multiplexer_1 (
    .in0(lt_out), .in1(3'b001), .in2(lt_out), .in4(3'b100), .out({o_lt, o_eq, o_gt}), .sel({i_lt, i_eq, i_gt}));  // open: in3, in5, in6, in7

  // Notes on the sheet:
  //   xx1
  //   x1x or 000
  //   1xx
  //   ->eq = normal cmp
  //   else = pass
  //   these are 'logic' from the prior gate, set 000 if start
endmodule

module cmp_16bit (
  input  [15:0] c1,
  input  [15:0] c0,
  input  i_gt,
  input  i_eq,
  input  i_lt,
  output o_gt,
  output o_eq,
  output o_lt
);

  wire cmp_4bit_1_o_eq, cmp_4bit_1_o_gt, cmp_4bit_1_o_lt, cmp_4bit_2_o_eq, cmp_4bit_2_o_gt, cmp_4bit_2_o_lt,
       cmp_4bit_3_o_eq, cmp_4bit_3_o_gt, cmp_4bit_3_o_lt;

  cmp_4bit cmp_4bit_1 (
    .c0(c0[15:12]), .c1(c1[15:12]), .i_gt(i_gt), .i_eq(i_eq), .i_lt(i_lt), .o_gt(cmp_4bit_1_o_gt),
    .o_eq(cmp_4bit_1_o_eq), .o_lt(cmp_4bit_1_o_lt));
  cmp_4bit cmp_4bit_2 (
    .c0(c0[11:8]), .c1(c1[11:8]), .i_gt(cmp_4bit_1_o_gt), .i_eq(cmp_4bit_1_o_eq), .i_lt(cmp_4bit_1_o_lt),
    .o_gt(cmp_4bit_2_o_gt), .o_eq(cmp_4bit_2_o_eq), .o_lt(cmp_4bit_2_o_lt));
  cmp_4bit cmp_4bit_3 (
    .c0(c0[7:4]), .c1(c1[7:4]), .i_gt(cmp_4bit_2_o_gt), .i_eq(cmp_4bit_2_o_eq), .i_lt(cmp_4bit_2_o_lt),
    .o_gt(cmp_4bit_3_o_gt), .o_eq(cmp_4bit_3_o_eq), .o_lt(cmp_4bit_3_o_lt));
  cmp_4bit cmp_4bit_4 (
    .c0(c0[3:0]), .c1(c1[3:0]), .i_gt(cmp_4bit_3_o_gt), .i_eq(cmp_4bit_3_o_eq), .i_lt(cmp_4bit_3_o_lt),
    .o_gt(o_gt), .o_eq(o_eq), .o_lt(o_lt));
endmodule

module cmp_4bit (
  input  [3:0] c0,
  input  [3:0] c1,
  input  i_gt,
  input  i_eq,
  input  i_lt,
  output o_gt,
  output o_eq,
  output o_lt
);

  wire cmp_1bit_1_o_eq, cmp_1bit_1_o_gt, cmp_1bit_1_o_lt, cmp_1bit_2_o_eq, cmp_1bit_2_o_gt, cmp_1bit_2_o_lt,
       cmp_1bit_3_o_eq, cmp_1bit_3_o_gt, cmp_1bit_3_o_lt;

  cmp_1bit cmp_1bit_1 (
    .c0(c0[3]), .c1(c1[3]), .i_gt(i_gt), .i_eq(i_eq), .i_lt(i_lt), .o_gt(cmp_1bit_1_o_gt),
    .o_eq(cmp_1bit_1_o_eq), .o_lt(cmp_1bit_1_o_lt));
  cmp_1bit cmp_1bit_2 (
    .c0(c0[2]), .c1(c1[2]), .i_gt(cmp_1bit_1_o_gt), .i_eq(cmp_1bit_1_o_eq), .i_lt(cmp_1bit_1_o_lt),
    .o_gt(cmp_1bit_2_o_gt), .o_eq(cmp_1bit_2_o_eq), .o_lt(cmp_1bit_2_o_lt));
  cmp_1bit cmp_1bit_3 (
    .c0(c0[1]), .c1(c1[1]), .i_gt(cmp_1bit_2_o_gt), .i_eq(cmp_1bit_2_o_eq), .i_lt(cmp_1bit_2_o_lt),
    .o_gt(cmp_1bit_3_o_gt), .o_eq(cmp_1bit_3_o_eq), .o_lt(cmp_1bit_3_o_lt));
  cmp_1bit cmp_1bit_4 (
    .c0(c0[0]), .c1(c1[0]), .i_gt(cmp_1bit_3_o_gt), .i_eq(cmp_1bit_3_o_eq), .i_lt(cmp_1bit_3_o_lt),
    .o_gt(o_gt), .o_eq(o_eq), .o_lt(o_lt));
endmodule
