// Logisim project barrel_shifter.circ as structural Verilog: 2 circuits, main circuit main
module main (
  input  [7:0] DATA_IN,
  input  LOAD_IN,
  input  LOAD_OUT,
  input  [2:0] SHAMT,
  input  DIR,
  input  ROT,
  input  CLK,
  output [7:0] DATA_OUT
);

  wire [7:0] IN_LATCH_q, SHIFTER_y;

  Register IN_LATCH (.D(DATA_IN), .en(LOAD_IN), .clk(CLK), .Q(IN_LATCH_q));  // open: clr
  barrel_shifter_8b SHIFTER (.D(IN_LATCH_q), .SHAMT(SHAMT), .DIR(DIR), .ROT(ROT), .Y(SHIFTER_y));
  Register OUT_LATCH (.D(SHIFTER_y), .en(LOAD_OUT), .clk(CLK), .Q(DATA_OUT));  // open: clr
endmodule

module barrel_shifter_8b (
  input  [7:0] D,
  input  [2:0] SHAMT,
  input  DIR,
  input  ROT,
  output [7:0] Y
);

  wire a0, a1, a2, a3, a4, a5, a6, a7, b0, b1, b2, b3, b4, b5, b6, b7, wL1_0, wL2_0, wL2_1, wL4_0, wL4_1,
       wL4_2, wL4_3, wR1_7, wR2_6, wR2_7, wR4_4, wR4_5, wR4_6, wR4_7;

  and and_1 (wL1_0, ROT, D[7]);
  and and_2 (wR1_7, ROT, D[0]);
  Multiplexer #(.select(2)) multiplexer_1 (
    .in0(D[0]), .in1(wL1_0), .in2(D[0]), .in3(D[1]), .out(a0), .sel({DIR, SHAMT[0]}));
  Multiplexer #(.select(2)) multiplexer_2 (
    .in0(D[1]), .in1(D[0]), .in2(D[1]), .in3(D[2]), .out(a1), .sel({DIR, SHAMT[0]}));
  Multiplexer #(.select(2)) multiplexer_3 (
    .in0(D[2]), .in1(D[1]), .in2(D[2]), .in3(D[3]), .out(a2), .sel({DIR, SHAMT[0]}));
  Multiplexer #(.select(2)) multiplexer_4 (
    .in0(D[3]), .in1(D[2]), .in2(D[3]), .in3(D[4]), .out(a3), .sel({DIR, SHAMT[0]}));
  Multiplexer #(.select(2)) multiplexer_5 (
    .in0(D[4]), .in1(D[3]), .in2(D[4]), .in3(D[5]), .out(a4), .sel({DIR, SHAMT[0]}));
  Multiplexer #(.select(2)) multiplexer_6 (
    .in0(D[5]), .in1(D[4]), .in2(D[5]), .in3(D[6]), .out(a5), .sel({DIR, SHAMT[0]}));
  Multiplexer #(.select(2)) multiplexer_7 (
    .in0(D[6]), .in1(D[5]), .in2(D[6]), .in3(D[7]), .out(a6), .sel({DIR, SHAMT[0]}));
  Multiplexer #(.select(2)) multiplexer_8 (
    .in0(D[7]), .in1(D[6]), .in2(D[7]), .in3(wR1_7), .out(a7), .sel({DIR, SHAMT[0]}));
  and and_3 (wL2_0, ROT, a6);
  and and_4 (wL2_1, ROT, a7);
  and and_5 (wR2_6, ROT, a0);
  and and_6 (wR2_7, ROT, a1);
  Multiplexer #(.select(2)) multiplexer_9 (.in0(a0), .in1(wL2_0), .in2(a0), .in3(a2), .out(b0), .sel({DIR, SHAMT[1]}));
  Multiplexer #(.select(2)) multiplexer_10 (.in0(a1), .in1(wL2_1), .in2(a1), .in3(a3), .out(b1), .sel({DIR, SHAMT[1]}));
  Multiplexer #(.select(2)) multiplexer_11 (.in0(a2), .in1(a0), .in2(a2), .in3(a4), .out(b2), .sel({DIR, SHAMT[1]}));
  Multiplexer #(.select(2)) multiplexer_12 (.in0(a3), .in1(a1), .in2(a3), .in3(a5), .out(b3), .sel({DIR, SHAMT[1]}));
  Multiplexer #(.select(2)) multiplexer_13 (.in0(a4), .in1(a2), .in2(a4), .in3(a6), .out(b4), .sel({DIR, SHAMT[1]}));
  Multiplexer #(.select(2)) multiplexer_14 (.in0(a5), .in1(a3), .in2(a5), .in3(a7), .out(b5), .sel({DIR, SHAMT[1]}));
  Multiplexer #(.select(2)) multiplexer_15 (.in0(a6), .in1(a4), .in2(a6), .in3(wR2_6), .out(b6), .sel({DIR, SHAMT[1]}));
  Multiplexer #(.select(2)) multiplexer_16 (.in0(a7), .in1(a5), .in2(a7), .in3(wR2_7), .out(b7), .sel({DIR, SHAMT[1]}));
  and and_7 (wL4_0, ROT, b4);
  and and_8 (wL4_1, ROT, b5);
  and and_9 (wL4_2, ROT, b6);
  and and_10 (wL4_3, ROT, b7);
  and and_11 (wR4_4, ROT, b0);
  and and_12 (wR4_5, ROT, b1);
  and and_13 (wR4_6, ROT, b2);
  and and_14 (wR4_7, ROT, b3);
  Multiplexer #(.select(2)) multiplexer_17 (
    .in0(b0), .in1(wL4_0), .in2(b0), .in3(b4), .out(Y[0]), .sel({DIR, SHAMT[2]}));
  Multiplexer #(.select(2)) multiplexer_18 (
    .in0(b1), .in1(wL4_1), .in2(b1), .in3(b5), .out(Y[1]), .sel({DIR, SHAMT[2]}));
  Multiplexer #(.select(2)) multiplexer_19 (
    .in0(b2), .in1(wL4_2), .in2(b2), .in3(b6), .out(Y[2]), .sel({DIR, SHAMT[2]}));
  Multiplexer #(.select(2)) multiplexer_20 (
    .in0(b3), .in1(wL4_3), .in2(b3), .in3(b7), .out(Y[3]), .sel({DIR, SHAMT[2]}));
  Multiplexer #(.select(2)) multiplexer_21 (
    .in0(b4), .in1(b0), .in2(b4), .in3(wR4_4), .out(Y[4]), .sel({DIR, SHAMT[2]}));
  Multiplexer #(.select(2)) multiplexer_22 (
    .in0(b5), .in1(b1), .in2(b5), .in3(wR4_5), .out(Y[5]), .sel({DIR, SHAMT[2]}));
  Multiplexer #(.select(2)) multiplexer_23 (
    .in0(b6), .in1(b2), .in2(b6), .in3(wR4_6), .out(Y[6]), .sel({DIR, SHAMT[2]}));
  Multiplexer #(.select(2)) multiplexer_24 (
    .in0(b7), .in1(b3), .in2(b7), .in3(wR4_7), .out(Y[7]), .sel({DIR, SHAMT[2]}));

  // Other names for the same wires on the sheet: s0 = SHAMT[0]; sel0[1:0] = {DIR, SHAMT[0]}; s1 = SHAMT[1];
  //   sel1[1:0] = {DIR, SHAMT[1]}; s2 = SHAMT[2]; sel2[1:0] = {DIR, SHAMT[2]}

  // Notes on the sheet:
  //   8-bit Left/Right Barrel Shifter (log shifter: stages of 1, 2, 4)
  //   DIR: 0 = left, 1 = right     ROT: 0 = logical shift (zero fill), 1 = rotate     SHAMT: 0-7
  //   Stage 0: shift by 1 (SHAMT bit 0)
  //   Stage 1: shift by 2 (SHAMT bit 1)
  //   Stage 2: shift by 4 (SHAMT bit 2)
endmodule
