// Logisim project main.circ as structural Verilog
module main (
);

  CPU_Unit cpu_unit_1 ();  // open: Ctrl, Addr, Data, in_4, in_5, out_6, out_7, out_8, out_9, out_10
  tri_state_buffer tri_state_buffer_1 ();
  ROM rom_1 ();  // open: addr, data
  RAM ram_1 ();  // open: addr, we, oe, clk, din, dout
  IO_Unit io_unit_1 ();  // open: in_1, in_2, in_3, in_4, in_5, in_6, in_7, in_8, in_9, out_10, out_11, out_12, out_13, out_14
endmodule

module CPU_Unit (
  input  Ctrl,
  input  Addr,
  input  Data,
  input  in_4,
  input  in_5,
  output out_6,
  output out_7,
  output out_8,
  output out_9,
  output out_10
);
endmodule

module Memory_Unit (
  input  in_1,
  input  in_2,
  input  in_3,
  input  in_4,
  input  in_5,
  output out_6
);
endmodule

module IO_Unit (
  input  in_1,
  input  in_2,
  input  in_3,
  input  in_4,
  input  in_5,
  input  in_6,
  input  in_7,
  input  in_8,
  input  in_9,
  output out_10,
  output out_11,
  output out_12,
  output out_13,
  output out_14
);
endmodule

module IO_Output (
  input  [3:0] W_data,
  input  [1:0] W_addr,
  input  [1:0] R_addr,
  input  W_en,
  input  R_en,
  output [3:0] R_data
);

  wire and_1_out, and_2_out, and_3_out, and_4_out, clk_out, clr_out, decoder_1_out0, decoder_1_out1,
       decoder_1_out2, decoder_1_out3;
  wire [3:0] register_1_q, register_2_q, register_3_q, register_4_q;

  Decoder #(.enable("false"), .select(2)) decoder_1 (
    .out0(decoder_1_out0), .out1(decoder_1_out1), .out2(decoder_1_out2), .out3(decoder_1_out3), .sel(W_addr));
  Button clk (.out(clk_out));
  and and_1 (and_1_out, decoder_1_out0, W_en);
  and and_2 (and_2_out, decoder_1_out1, W_en);
  and and_3 (and_3_out, decoder_1_out2, W_en);
  and and_4 (and_4_out, decoder_1_out3, W_en);
  Button clr (.out(clr_out));
  Register #(.width(4)) register_1 (.D(W_data), .en(and_1_out), .clk(clk_out), .Q(register_1_q), .clr(clr_out));
  Register #(.width(4)) register_2 (.D(W_data), .en(and_2_out), .clk(clk_out), .Q(register_2_q), .clr(clr_out));
  Register #(.width(4)) register_3 (.D(W_data), .en(and_3_out), .clk(clk_out), .Q(register_3_q), .clr(clr_out));
  Register #(.width(4)) register_4 (.D(W_data), .en(and_4_out), .clk(clk_out), .Q(register_4_q), .clr(clr_out));
  Multiplexer #(.enable("true"), .select(2), .width(4)) multiplexer_1 (
    .in0(register_1_q), .in1(register_2_q), .in2(register_3_q), .in3(register_4_q), .out(R_data),
    .sel(R_addr), .en(R_en));
endmodule
