// Logisim project p1.circ as structural Verilog: 7 circuits, main circuit main
module main (
  input  [7:0] Ctrl,
  input  [7:0] Addr,
  input  [7:0] Data,
  input  Enable,
  output [7:0] o00,
  output [7:0] o01,
  output [7:0] o10,
  output [7:0] o11,
  output [7:0] Ctrl_Cur,
  output [7:0] Addr_Cur,
  output [7:0] Data_Cur
);

  wire Clk_out;

  Clock Clk (.out(Clk_out));
  CPU cpu_1 (
    .Control(Ctrl), .Address(Addr), .Data_Wr(Data), .Enable(Enable), .Control_Out(Ctrl_Cur),
    .Address_Out(Addr_Cur), .Wr_Out(Data_Cur));  // open: Data_Read, Rd_Out
  mem_unit mem_unit_1 (
    .Data_In(Data_Cur), .Address(Addr_Cur), .Control(Ctrl_Cur), .Enable(Enable), .Clk(Clk_out),
    .Data_Out(Data_Cur));
  IO_Sys IO (
    .Clk(Clk_out), .Control(Ctrl_Cur), .Address(Addr_Cur), .Enable(Enable), .Data_In(Data_Cur), .o00(o00),
    .o01(o01), .o10(o10), .o11(o11), .Data_Out(Data_Cur));  // open: R

  // Notes on the sheet:
  //   10xx: RAM
  //   01xx: ROM
  //   Small Control Guide:
  //   MEMORY R/W
  //   xx01: (MEM) READ
  //   xx00: (MEM) WR
  //   +Addr = 8-bit Address
  //   Control
  //   Address
  //   Data
  //   Both: +Data = To-WR
  //   IO R/W
  //   xx11: (IO) READ
  //   xx00: (IO) WR
  //   +Addr = IO Device
endmodule

module tri_buffer (
  input  c,
  input  [7:0] i,
  output [7:0] o
);

  wire not_1_out;

  not not_1 (not_1_out, c);
  Transistor #(.width(8)) transistor_1 (.in(i), .out(o), .gate(not_1_out));
  Transistor #(.\type ("n"), .width(8)) transistor_2 (.in(i), .out(o), .gate(c));

  // Notes on the sheet:
  //   8-bit tri state buffer
endmodule

module CPU (
  input  [7:0] Control,
  input  [7:0] Address,
  input  [7:0] Data_Wr,
  input  [7:0] Data_Read,
  input  Enable,
  output [7:0] Control_Out,
  output [7:0] Address_Out,
  output [7:0] Wr_Out,
  output [7:0] Rd_Out
);

  wire [7:0] rd_wr_buffer_1_data_out;

  tri_buffer tri_buffer_1 (.i(Control), .c(Enable), .o(Control_Out));
  tri_buffer tri_buffer_2 (.i(Address), .c(Enable), .o(Address_Out));
  rd_wr_buffer rd_wr_buffer_1 (.Data_In(Data_Wr), .Control(Control), .Data_Out(rd_wr_buffer_1_data_out));
  tri_buffer tri_buffer_3 (.i(rd_wr_buffer_1_data_out), .c(Enable), .o(Wr_Out));
  tri_buffer tri_buffer_4 (.i(Data_Read), .c(Enable), .o(Rd_Out));

  // Notes on the sheet:
  //   CPU writes to Data on RD
endmodule

module IO_Sys (
  input  Enable,
  input  [7:0] Data_In,
  input  Clk,
  input  R,
  input  [7:0] Control,
  input  [7:0] Address,
  output [7:0] o00,
  output [7:0] Data_Out,
  output [7:0] o01,
  output [7:0] o10,
  output [7:0] o11
);

  wire and_1_out, and_2_out, and_3_out, and_4_out, and_5_out, and_6_out, and_7_out, and_8_out, and_9_out,
       and_10_out, decoder_1_out0, decoder_1_out1, decoder_1_out2, decoder_1_out3, not_1_out, not_2_out,
       not_3_out, not_4_out, not_5_out;
  wire [7:0] tri_buffer_1_o;

  not not_1 (not_1_out, Control[0]);
  and and_1 (and_1_out, Enable, Control[1]);
  Decoder #(.select(2)) decoder_1 (
    .out0(decoder_1_out0), .out1(decoder_1_out1), .out2(decoder_1_out2), .out3(decoder_1_out3),
    .sel(Address[1:0]), .en(and_1_out));
  // NoConnect on Address[7:2]
  and and_2 (and_2_out, and_1_out, not_1_out);
  not not_2 (not_2_out, not_1_out);
  and and_3 (and_3_out, not_2_out, decoder_1_out0, and_1_out);
  and and_4 (and_4_out, not_1_out, decoder_1_out0, and_1_out);
  not not_3 (not_3_out, not_1_out);
  and and_5 (and_5_out, not_3_out, decoder_1_out1, and_1_out);
  and and_6 (and_6_out, not_1_out, decoder_1_out1, and_1_out);
  not not_4 (not_4_out, not_1_out);
  and and_7 (and_7_out, not_4_out, decoder_1_out2, and_1_out);
  and and_8 (and_8_out, not_1_out, decoder_1_out2, and_1_out);
  not not_5 (not_5_out, not_1_out);
  and and_9 (and_9_out, not_5_out, decoder_1_out3, and_1_out);
  and and_10 (and_10_out, not_1_out, decoder_1_out3, and_1_out);
  Register i00 (.D(tri_buffer_1_o), .en(and_4_out), .clk(Clk), .Q(o00), .clr(R));
  tri_buffer tri_buffer_1 (.i(Data_In), .c(and_2_out), .o(tri_buffer_1_o));
  Register i01 (.D(tri_buffer_1_o), .en(and_6_out), .clk(Clk), .Q(o01), .clr(R));
  Register i10 (.D(tri_buffer_1_o), .en(and_8_out), .clk(Clk), .Q(o10), .clr(R));
  Register i11 (.D(tri_buffer_1_o), .en(and_10_out), .clk(Clk), .Q(o11), .clr(R));
  tri_buffer tri_buffer_2 (.i(o00), .c(and_3_out), .o(Data_Out));
  tri_buffer tri_buffer_3 (.i(o01), .c(and_5_out), .o(Data_Out));
  tri_buffer tri_buffer_4 (.i(o10), .c(and_7_out), .o(Data_Out));
  tri_buffer tri_buffer_5 (.i(o11), .c(and_9_out), .o(Data_Out));

  // Notes on the sheet:
  //   Should Activate
  //   WR
  //   decoded
  //   should rewrite as IO = register + (Async?) Set if reused in future lab
endmodule

module mem_unit (
  input  [7:0] Data_In,
  input  [7:0] Address,
  input  [7:0] Control,
  input  Enable,
  input  Clk,
  output [7:0] Data_Out
);

  wire C_out, C_RAM_out, C_ROM_out, not_1_out, not_2_out;
  wire [7:0] ram_1_dout, rom_1_data;

  // NoConnect on Control[7:4]
  ROM rom_1 (.addr(Address), .data(rom_1_data));
  not not_1 (not_1_out, Control[1]);
  and C (C_out, not_1_out, Enable);
  // NoConnect on not_1_out
  // NoConnect on Control[2]
  // NoConnect on Control[3]
  tri_buffer tri_buffer_1 (.i(rom_1_data), .c(C_ROM_out), .o(Data_Out));
  and C_RAM (C_RAM_out, Control[3], Control[0], C_out);
  and C_ROM (C_ROM_out, C_out, Control[2]);
  RAM ram_1 (.addr(Address), .we(not_2_out), .oe(Control[0]), .clk(Clk), .din(Data_In), .dout(ram_1_dout));
  not not_2 (not_2_out, Control[0]);
  tri_buffer tri_buffer_2 (.i(ram_1_dout), .c(C_RAM_out), .o(Data_Out));

  // Notes on the sheet:
  //   0: 0/1 = WR/RD
  //   1: IO/M-low
  //   2: C_ROM
  //   3: C_RAM
  //   contents of rom_1 (hex, n*v repeats v):
  //   0 1 2 3 4 5 6 7 8 9 10 11 12 13 14 15
  //   only used by ram
  //   WR (0), RD (1)
  //   RAM Control
  //   ROM Control
  //   Clk
  //   invalid read until first clk (unspecified ptr)
endmodule

module rd_wr_buffer (
  input  [7:0] Data_In,
  input  [7:0] Control,
  output [7:0] Data_Out
);

  wire not_1_out;

  // NoConnect on Control[7:1]
  not not_1 (not_1_out, Control[0]);
  tri_buffer tri_buffer_1 (.i(Data_In), .c(not_1_out), .o(Data_Out));

  // Notes on the sheet:
  //   CTRL Bit 0 :: 0/1 = WR/RD
  //   just crops 8-bit control into rd/wr based buffer
endmodule

module tri_buffer1b (
  input  c,
  input  i,
  output o
);

  wire not_1_out;

  not not_1 (not_1_out, c);
  Transistor transistor_1 (.in(i), .out(o), .gate(not_1_out));
  Transistor #(.\type ("n")) transistor_2 (.in(i), .out(o), .gate(c));

  // Notes on the sheet:
  //   1-bit tri-state buffer
endmodule
