// Logisim project problem2.circ as structural Verilog: 4 circuits, main circuit main
module main (
  input  A7,
  input  A6,
  input  A5,
  input  A4,
  input  A3,
  input  A2,
  input  A1,
  input  A0,
  input  B7,
  input  B6,
  input  B5,
  input  B4,
  input  B3,
  input  B2,
  input  B1,
  input  B0,
  output Greater,
  output Equal,
  output Less
);

  wire eightbitsubtractor_1_cout, eightbitsubtractor_1_s0, eightbitsubtractor_1_s1, eightbitsubtractor_1_s2,
       eightbitsubtractor_1_s3, eightbitsubtractor_1_s4, eightbitsubtractor_1_s5, eightbitsubtractor_1_s6,
       eightbitsubtractor_1_s7, nor_1_out, nor_2_out, not_1_out, not_2_out;

  EightBitSubtractor eightbitsubtractor_1 (
    .A7(A7), .A6(A6), .A5(A5), .A4(A4), .A3(A3), .A2(A2), .A1(A1), .A0(A0), .B7(B7), .B6(B6), .B5(B5),
    .B4(B4), .B3(B3), .B2(B2), .B1(B1), .B0(B0), .S7(eightbitsubtractor_1_s7), .S6(eightbitsubtractor_1_s6),
    .S5(eightbitsubtractor_1_s5), .S4(eightbitsubtractor_1_s4), .S3(eightbitsubtractor_1_s3),
    .S2(eightbitsubtractor_1_s2), .S1(eightbitsubtractor_1_s1), .S0(eightbitsubtractor_1_s0),
    .Cout(eightbitsubtractor_1_cout));
  nor nor_1 (nor_1_out, eightbitsubtractor_1_s7, eightbitsubtractor_1_s6, eightbitsubtractor_1_s5, eightbitsubtractor_1_s4);
  nor nor_2 (nor_2_out, eightbitsubtractor_1_s3, eightbitsubtractor_1_s2, eightbitsubtractor_1_s1, eightbitsubtractor_1_s0);
  and and_1 (Equal, nor_1_out, nor_2_out);
  not not_1 (not_1_out, Equal);
  and and_2 (Greater, not_1_out, eightbitsubtractor_1_cout);
  and and_3 (Less, not_1_out, not_2_out);
  not not_2 (not_2_out, eightbitsubtractor_1_cout);
endmodule

module FullAdder (
  input  A,
  input  B,
  input  Cin,
  output S,
  output Cout
);

  wire and_1_out, and_2_out, xor_1_out;

  xor xor_1 (xor_1_out, A, B);
  xor xor_2 (S, xor_1_out, Cin);
  and and_1 (and_1_out, Cin, xor_1_out);
  and and_2 (and_2_out, B, A);
  or or_1 (Cout, and_1_out, and_2_out);
endmodule

module EightBitAdder (
  input  A7,
  input  A6,
  input  A5,
  input  A4,
  input  A3,
  input  A2,
  input  A1,
  input  A0,
  input  B7,
  input  B6,
  input  B5,
  input  B4,
  input  B3,
  input  B2,
  input  B1,
  input  B0,
  input  Cin,
  output S7,
  output S6,
  output S5,
  output S4,
  output S3,
  output S2,
  output S1,
  output S0,
  output Cout
);

  wire fulladder_1_cout, fulladder_2_cout, fulladder_3_cout, fulladder_4_cout, fulladder_5_cout,
       fulladder_6_cout, fulladder_7_cout;

  FullAdder fulladder_1 (.A(A0), .B(B0), .Cin(Cin), .S(S0), .Cout(fulladder_1_cout));
  FullAdder fulladder_2 (.A(A1), .B(B1), .Cin(fulladder_1_cout), .S(S1), .Cout(fulladder_2_cout));
  FullAdder fulladder_3 (.A(A2), .B(B2), .Cin(fulladder_2_cout), .S(S2), .Cout(fulladder_3_cout));
  FullAdder fulladder_4 (.A(A3), .B(B3), .Cin(fulladder_3_cout), .S(S3), .Cout(fulladder_4_cout));
  FullAdder fulladder_5 (.A(A4), .B(B4), .Cin(fulladder_4_cout), .S(S4), .Cout(fulladder_5_cout));
  FullAdder fulladder_6 (.A(A5), .B(B5), .Cin(fulladder_5_cout), .S(S5), .Cout(fulladder_6_cout));
  FullAdder fulladder_7 (.A(A6), .B(B6), .Cin(fulladder_6_cout), .S(S6), .Cout(fulladder_7_cout));
  FullAdder fulladder_8 (.A(A7), .B(B7), .Cin(fulladder_7_cout), .S(S7), .Cout(Cout));
endmodule

module EightBitSubtractor (
  input  A7,
  input  A6,
  input  A5,
  input  A4,
  input  A3,
  input  A2,
  input  A1,
  input  A0,
  input  B7,
  input  B6,
  input  B5,
  input  B4,
  input  B3,
  input  B2,
  input  B1,
  input  B0,
  output S7,
  output S6,
  output S5,
  output S4,
  output S3,
  output S2,
  output S1,
  output S0,
  output Cout
);

  wire not_1_out, not_2_out, not_3_out, not_4_out, not_5_out, not_6_out, not_7_out, not_8_out;

  not not_1 (not_1_out, B7);
  not not_2 (not_2_out, B6);
  not not_3 (not_3_out, B5);
  not not_4 (not_4_out, B4);
  not not_5 (not_5_out, B3);
  not not_6 (not_6_out, B2);
  not not_7 (not_7_out, B1);
  not not_8 (not_8_out, B0);
  EightBitAdder eightbitadder_1 (
    .A7(A7), .A6(A6), .A5(A5), .A4(A4), .A3(A3), .A2(A2), .A1(A1), .A0(A0), .B7(not_1_out), .B6(not_2_out),
    .B5(not_3_out), .B4(not_4_out), .B3(not_5_out), .B2(not_6_out), .B1(not_7_out), .B0(not_8_out),
    .Cin(1'b1), .S7(S7), .S6(S6), .S5(S5), .S4(S4), .S3(S3), .S2(S2), .S1(S1), .S0(S0), .Cout(Cout));
endmodule
