// Logisim project problem3.circ as structural Verilog: 8 circuits, main circuit main
module main (
  input  Left,
  input  Right
);

  wire CLK_out, leddecoder_1_led0, leddecoder_1_led1, leddecoder_1_led2, leddecoder_1_led3,
       leddecoder_1_led4, leddecoder_1_led5, leddecoder_1_led6, leddecoder_1_led7, leddecoder_1_led8,
       leddecoder_1_led9, leddecoder_1_led10, leddecoder_1_led11, leddecoder_1_led12, leddecoder_1_led13,
       leddecoder_1_led14, leddecoder_1_led15, leddecoder_1_led16, leddecoder_1_led17, leddecoder_1_led18,
       leddecoder_1_led19, twowaycounter_1_q0, twowaycounter_1_q1, twowaycounter_1_q2, twowaycounter_1_q3,
       twowaycounter_1_q4;

  Clock CLK (.out(CLK_out));
  LED led_1 (.in(leddecoder_1_led0));
  LEDdecoder leddecoder_1 (
    .Q0(twowaycounter_1_q0), .Q1(twowaycounter_1_q1), .Q2(twowaycounter_1_q2), .Q3(twowaycounter_1_q3),
    .Q4(twowaycounter_1_q4), .LED0(leddecoder_1_led0), .LED1(leddecoder_1_led1), .LED2(leddecoder_1_led2),
    .LED3(leddecoder_1_led3), .LED4(leddecoder_1_led4), .LED5(leddecoder_1_led5), .LED6(leddecoder_1_led6),
    .LED7(leddecoder_1_led7), .LED8(leddecoder_1_led8), .LED9(leddecoder_1_led9), .LED10(leddecoder_1_led10),
    .LED11(leddecoder_1_led11), .LED12(leddecoder_1_led12), .LED13(leddecoder_1_led13),
    .LED14(leddecoder_1_led14), .LED15(leddecoder_1_led15), .LED16(leddecoder_1_led16),
    .LED17(leddecoder_1_led17), .LED18(leddecoder_1_led18), .LED19(leddecoder_1_led19));
  TwoWayCounter twowaycounter_1 (
    .Left(Left), .Right(Right), .CLK(CLK_out), .Q0(twowaycounter_1_q0), .Q1(twowaycounter_1_q1),
    .Q2(twowaycounter_1_q2), .Q3(twowaycounter_1_q3), .Q4(twowaycounter_1_q4));
  LED led_2 (.in(leddecoder_1_led1));
  LED led_3 (.in(leddecoder_1_led2));
  LED led_4 (.in(leddecoder_1_led3));
  LED led_5 (.in(leddecoder_1_led4));
  LED led_6 (.in(leddecoder_1_led5));
  LED led_7 (.in(leddecoder_1_led6));
  LED led_8 (.in(leddecoder_1_led7));
  LED led_9 (.in(leddecoder_1_led8));
  LED led_10 (.in(leddecoder_1_led9));
  LED led_11 (.in(leddecoder_1_led10));
  LED led_12 (.in(leddecoder_1_led11));
  LED led_13 (.in(leddecoder_1_led12));
  LED led_14 (.in(leddecoder_1_led13));
  LED led_15 (.in(leddecoder_1_led14));
  LED led_16 (.in(leddecoder_1_led15));
  LED led_17 (.in(leddecoder_1_led16));
  LED led_18 (.in(leddecoder_1_led17));
  LED led_19 (.in(leddecoder_1_led18));
  LED led_20 (.in(leddecoder_1_led19));
endmodule

module LEDdecoder (
  input  Q0,
  input  Q1,
  input  Q2,
  input  Q3,
  input  Q4,
  output LED0,
  output LED1,
  output LED2,
  output LED3,
  output LED4,
  output LED5,
  output LED6,
  output LED7,
  output LED8,
  output LED9,
  output LED10,
  output LED11,
  output LED12,
  output LED13,
  output LED14,
  output LED15,
  output LED16,
  output LED17,
  output LED18,
  output LED19
);

  wire not_1_out, not_2_out, not_3_out, not_4_out, not_5_out;

  not not_1 (not_1_out, Q0);
  not not_2 (not_2_out, Q1);
  not not_3 (not_3_out, Q2);
  not not_4 (not_4_out, Q3);
  not not_5 (not_5_out, Q4);
  and and_1 (LED0, not_5_out, not_4_out, not_3_out, not_2_out, not_1_out);
  and and_2 (LED1, not_5_out, not_4_out, not_3_out, not_2_out, Q0);
  and and_3 (LED2, not_5_out, not_4_out, not_3_out, Q1, not_1_out);
  and and_4 (LED3, not_5_out, not_4_out, not_3_out, Q1, Q0);
  and and_5 (LED4, not_5_out, not_4_out, Q2, not_2_out, not_1_out);
  and and_6 (LED5, not_5_out, not_4_out, Q2, not_2_out, Q0);
  and and_7 (LED6, not_5_out, not_4_out, Q2, Q1, not_1_out);
  and and_8 (LED7, not_5_out, not_4_out, Q2, Q1, Q0);
  and and_9 (LED8, not_5_out, Q3, not_3_out, not_2_out, not_1_out);
  and and_10 (LED9, not_5_out, Q3, not_3_out, not_2_out, Q0);
  and and_11 (LED10, not_5_out, Q3, not_3_out, Q1, not_1_out);
  and and_12 (LED12, not_5_out, Q3, Q2, not_2_out, not_1_out);
  and and_13 (LED11, not_5_out, Q3, not_3_out, Q1, Q0);
  and and_14 (LED13, not_5_out, Q3, Q2, not_2_out, Q0);
  and and_15 (LED14, not_5_out, Q3, Q2, Q1, not_1_out);
  and and_16 (LED15, not_5_out, Q3, Q2, Q1, Q0);
  and and_17 (LED16, Q4, not_4_out, not_3_out, not_2_out, not_1_out);
  and and_18 (LED17, Q4, not_4_out, not_3_out, not_2_out, Q0);
  and and_19 (LED18, Q4, not_4_out, not_3_out, Q1, not_1_out);
  and and_20 (LED19, Q4, not_4_out, not_3_out, Q1, Q0);
endmodule

module TwoWayCounter (
  input  Left,
  input  Right,
  input  CLK,
  output Q0,
  output Q1,
  output Q2,
  output Q3,
  output Q4
);

  wire fivebitadder_1_s0, fivebitadder_1_s1, fivebitadder_1_s2, fivebitadder_1_s3, fivebitadder_1_s4,
       or_1_out, wraparoundlogic_1_d0, wraparoundlogic_1_d1, wraparoundlogic_1_d2, wraparoundlogic_1_d3,
       wraparoundlogic_1_d4;

  D_Flip_Flop d_ff_1 (.D(wraparoundlogic_1_d4), .clk(CLK), .Q(Q4));  // open: Qn, preset, reset
  D_Flip_Flop d_ff_2 (.D(wraparoundlogic_1_d3), .clk(CLK), .Q(Q3));  // open: Qn, preset, reset
  D_Flip_Flop d_ff_3 (.D(wraparoundlogic_1_d2), .clk(CLK), .Q(Q2));  // open: Qn, preset, reset
  D_Flip_Flop d_ff_4 (.D(wraparoundlogic_1_d1), .clk(CLK), .Q(Q1));  // open: Qn, preset, reset
  D_Flip_Flop d_ff_5 (.D(wraparoundlogic_1_d0), .clk(CLK), .Q(Q0));  // open: Qn, preset, reset
  or or_1 (or_1_out, Right, Left);
  FiveBitAdder fivebitadder_1 (
    .A4(Q4), .A3(Q3), .A2(Q2), .A1(Q1), .A0(Q0), .B4(Left), .B3(Left), .B2(Left), .B1(Left), .B0(or_1_out),
    .S4(fivebitadder_1_s4), .S3(fivebitadder_1_s3), .S2(fivebitadder_1_s2), .S1(fivebitadder_1_s1),
    .S0(fivebitadder_1_s0));
  WrapAroundLogic wraparoundlogic_1 (
    .S4(fivebitadder_1_s4), .S3(fivebitadder_1_s3), .S2(fivebitadder_1_s2), .S1(fivebitadder_1_s1),
    .S0(fivebitadder_1_s0), .D4(wraparoundlogic_1_d4), .D3(wraparoundlogic_1_d3), .D2(wraparoundlogic_1_d2),
    .D1(wraparoundlogic_1_d1), .D0(wraparoundlogic_1_d0));
endmodule

module OneBitAdder (
  input  A,
  input  B,
  input  C,
  output S,
  output C_out
);

  wire and_1_out, and_2_out, xor_1_out;

  xor xor_1 (xor_1_out, A, B);
  and and_1 (and_1_out, A, B);
  xor xor_2 (S, xor_1_out, C);
  and and_2 (and_2_out, xor_1_out, C);
  or or_1 (C_out, and_2_out, and_1_out);
endmodule

module FiveBitAdder (
  input  A4,
  input  A3,
  input  A2,
  input  A1,
  input  A0,
  input  B4,
  input  B3,
  input  B2,
  input  B1,
  input  B0,
  output S4,
  output S3,
  output S2,
  output S1,
  output S0
);

  wire onebitadder_1_c_out, onebitadder_2_c_out, onebitadder_3_c_out, onebitadder_4_c_out;

  OneBitAdder onebitadder_1 (.A(A0), .B(B0), .C(1'b0), .S(S0), .C_out(onebitadder_1_c_out));
  OneBitAdder onebitadder_2 (.A(A1), .B(B1), .C(onebitadder_1_c_out), .S(S1), .C_out(onebitadder_2_c_out));
  OneBitAdder onebitadder_3 (.A(A2), .B(B2), .C(onebitadder_2_c_out), .S(S2), .C_out(onebitadder_3_c_out));
  OneBitAdder onebitadder_4 (.A(A3), .B(B3), .C(onebitadder_3_c_out), .S(S3), .C_out(onebitadder_4_c_out));
  OneBitAdder onebitadder_5 (.A(A4), .B(B4), .C(onebitadder_4_c_out), .S(S4));  // open: C_out
endmodule

module WrapAroundLogic (
  input  S4,
  input  S3,
  input  S2,
  input  S1,
  input  S0,
  output D4,
  output D3,
  output D2,
  output D1,
  output D0
);

  wire and_1_out, and_2_out, nor_1_out, not_2_out, not_4_out, not_5_out;

  // NOT_Gate not_1 has open pins: in=S4, out=open
  not not_2 (not_2_out, S3);
  // NOT_Gate not_3 has open pins: in=S2, out=open
  not not_4 (not_4_out, S1);
  not not_5 (not_5_out, S0);
  and and_1 (and_1_out, not_5_out, not_4_out, S2, not_2_out, S4);
  and and_2 (and_2_out, S0, S1, S2, S3, S4);
  nor nor_1 (nor_1_out, and_2_out, and_1_out);
  WrapHelper wraphelper_1 (.Si(S0), .P(nor_1_out), .E31(and_2_out), .Di(D0));
  WrapHelper wraphelper_2 (.Si(S1), .P(nor_1_out), .E31(and_2_out), .Di(D1));
  WrapHelper wraphelper_3 (.Si(S2), .P(nor_1_out), .E31(1'b0), .Di(D2));
  WrapHelper wraphelper_4 (.Si(S3), .P(nor_1_out), .E31(1'b0), .Di(D3));
  WrapHelper wraphelper_5 (.Si(S4), .P(nor_1_out), .E31(and_2_out), .Di(D4));
endmodule

module WrapHelper (
  input  Si,
  input  P,
  input  E31,
  output Di
);

  wire and_1_out;

  and and_1 (and_1_out, Si, P);
  or or_1 (Di, and_1_out, E31);
endmodule

module mainWithROM (
  input  Left,
  input  Right
);

  wire CLK_out;
  wire [4:0] twowaycounter_1_q0;
  wire [19:0] rom_1_data;

  Clock CLK (.out(CLK_out));
  LED led_1 (.in(rom_1_data[0]));
  TwoWayCounter twowaycounter_1 (
    .Left(Left), .Right(Right), .CLK(CLK_out), .Q0(twowaycounter_1_q0[0]), .Q1(twowaycounter_1_q0[1]),
    .Q2(twowaycounter_1_q0[2]), .Q3(twowaycounter_1_q0[3]), .Q4(twowaycounter_1_q0[4]));
  LED led_2 (.in(rom_1_data[1]));
  LED led_3 (.in(rom_1_data[2]));
  LED led_4 (.in(rom_1_data[3]));
  LED led_5 (.in(rom_1_data[4]));
  LED led_6 (.in(rom_1_data[5]));
  LED led_7 (.in(rom_1_data[6]));
  LED led_8 (.in(rom_1_data[7]));
  LED led_9 (.in(rom_1_data[8]));
  ROM #(.addrWidth(5), .dataWidth(20)) rom_1 (.addr(twowaycounter_1_q0), .data(rom_1_data));
  LED led_10 (.in(rom_1_data[9]));
  LED led_11 (.in(rom_1_data[10]));
  LED led_12 (.in(rom_1_data[11]));
  LED led_13 (.in(rom_1_data[12]));
  LED led_14 (.in(rom_1_data[13]));
  LED led_15 (.in(rom_1_data[14]));
  LED led_16 (.in(rom_1_data[15]));
  LED led_17 (.in(rom_1_data[16]));
  LED led_18 (.in(rom_1_data[17]));
  LED led_19 (.in(rom_1_data[18]));
  LED led_20 (.in(rom_1_data[19]));

  // Notes on the sheet:
  //   contents of rom_1 (hex, n*v repeats v):
  //   1 2 4 8 10 20 40 80 100 200 400 800 1000 2000 4000 8000 10000 20000 40000 80000
endmodule
